# Fritzing sketch AIM65 (saved by Fritzing 0.9.9b)

parts:
  Bauteil1 = Arduino Mega 2560 (Rev3)
  microSD1 = MicroSD Card Module

nets:
  N1: Bauteil1.5V, microSD1.CS
  N2: Bauteil1.GND, microSD1.SCK
  N3: Bauteil1.D50, microSD1.GND
  N4: Bauteil1.D51, microSD1.VCC
  N5: Bauteil1.D52, microSD1.MOSI
  N6: Bauteil1.D53, microSD1.MISO

notes:
  PS2 connector
  SPI
  I2C clock
  Serial printer
