# Fritzing sketch shieldmod2 (saved by Fritzing 0.9.9b)

parts:
  Bauteil1 = Arduino Prototyping Shield

nets:
  N1: Bauteil1.D8, Bauteil1.D10
  N2: Bauteil1.SDA, Bauteil1.A4
  N3: Bauteil1.SCL, Bauteil1.A5
